# Fritzing sketch synth-pants-fritzing (saved by Fritzing 1.0.2b)
breadboards: 1

parts:
  R1 = 220 Ω Resistor [package=THT]
  R2 = Resistor [tolerance=±5% resistance=1.5M package="2512 [SMD]"]
  Arduino_Uno = Arduino Uno (Rev3) - ICSP
  R4 = Resistor [tolerance=±5% resistance=47k package="2512 [SMD]"]
  R5 = Resistor [tolerance=±5% resistance=2.2k package="2512 [SMD]"]
  HC-06 = Bluetooth HC-05 Macho
  R6 = 220 Ω Resistor [package=THT]
  R9 = Resistor [tolerance=±5% resistance=1.5M package="2512 [SMD]"]
  R11 = Resistor [tolerance=±5% resistance=1.5M package="2512 [SMD]"]
  Sit_Sensor_1_(Pin_3) = female pin header, 1 pin [form="♀ (female)"]
  Cap_Sensor_(Pin_2) = female pin header, 1 pin [form="♀ (female)"]
  Knee_Sensor_1_(A1) = female pin header, 1 pin [form="♀ (female)"]
  Knee_Sensor_2_(A2) = female pin header, 1 pin [form="♀ (female)"]
  Sit_Sensor_2_(Pin_5) = female pin header, 1 pin [form="♀ (female)"]
  Knee_Sensor_1_OUT_(A1) = female pin header, 1 pin [form="♀ (female)"]
  Knee_Sensor_2_OUT_(A2) = female pin header, 1 pin [form="♀ (female)"]
  Walk_Sensor_(A0) = female pin header, 1 pin [form="♀ (female)"]

nets:
  N1: R1.330_Resistor, Arduino_Uno.A1, Knee_Sensor_1_(A1).pin1
  GND: R1.Pin_1, Arduino_Uno.GND, R4.Pin_1, HC-06.GND, R6.Pin_1
  N2: R2.Pin_0, Arduino_Uno.D2, Cap_Sensor_(Pin_2).pin1
  5V: R2.Pin_1, Arduino_Uno.5V, HC-06.VCC, R9.Pin_1, R11.Pin_1, Knee_Sensor_1_OUT_(A1).pin1, Knee_Sensor_2_OUT_(A2).pin1
  N3: Arduino_Uno.A0, Walk_Sensor_(A0).pin1
  N4: Arduino_Uno.A2, R6.330_Resistor, Knee_Sensor_2_(A2).pin1
  N5: Arduino_Uno.D8, R5.Pin_0
  N6: Arduino_Uno.D9_PWM, HC-06.RXD
  N7: Arduino_Uno.D3_PWM, R9.Pin_0, Sit_Sensor_1_(Pin_3).pin1
  N8: Arduino_Uno.D5_PWM, R11.Pin_0, Sit_Sensor_2_(Pin_5).pin1
  N9: R4.Pin_0, R5.Pin_1, HC-06.TXD

notes:
  KNEE (A1)
  capacitive (2)
  SIT (3)
  HC-06
  KNEE (A2)
  SIT (5)
  KNEE A1 OUT
  KNEE A2 OUT
  WALK (A0)

custom parts:
  220 Ω Resistor: A generic resistor (0.25W)
